// Logisim project cpu.circ as structural Verilog: 4 circuits, main circuit RISCV32
module ALU32 (
  input  [2:0] alu_op,
  input  [31:0] in_A,
  input  [31:0] in_B,
  output c,
  output [31:0] alu_out,
  output zero
);

  wire comparator_1_eq, comparator_1_gt, comparator_1_lt, multiplexer_1_out, not_1_out;
  wire [5:0] bitadder_1_out;
  wire [31:0] adder_1_out, and_1_out, bit_extender_1_out, multiplexer_2_out, or_1_out, subtractor_1_out;

  Adder #(.width(32)) adder_1 (.a(in_A), .b(in_B), .out(adder_1_out), .cin(1'b0), .cout(c));
  Subtractor #(.width(32)) subtractor_1 (.a(in_A), .b(in_B), .out(subtractor_1_out), .bin(1'b0));  // open: bout
  assign and_1_out = in_A & in_B;  // AND_Gate and_1, 32 bits wide
  assign or_1_out = in_A | in_B;  // OR_Gate or_1, 32 bits wide
  Comparator #(.width(32)) comparator_1 (
    .a(in_A), .b(in_B), .gt(comparator_1_gt), .eq(comparator_1_eq), .lt(comparator_1_lt));
  Multiplexer #(.select(3), .enable("false")) multiplexer_1 (
    .in0(1'b0), .in1(1'b0), .in2(1'b0), .in3(1'b0), .in4(comparator_1_gt), .in5(comparator_1_eq),
    .in6(not_1_out), .in7(comparator_1_lt), .out(multiplexer_1_out), .sel(alu_op));
  not not_1 (not_1_out, comparator_1_eq);
  Multiplexer #(.select(3), .width(32), .enable("false")) multiplexer_2 (
    .in0(adder_1_out), .in1(subtractor_1_out), .in2(and_1_out), .in3(or_1_out), .in4({32{1'b0}}),
    .in5({32{1'b0}}), .in6({32{1'b0}}), .in7({32{1'b0}}), .out(multiplexer_2_out), .sel(alu_op));
  assign bit_extender_1_out = {{31{1'b0}}, multiplexer_1_out};  // Bit_Extender bit_extender_1
  Multiplexer #(.width(32), .enable("false")) multiplexer_3 (
    .in0(multiplexer_2_out), .in1(bit_extender_1_out), .out(alu_out), .sel(alu_op[2]));
  and and_2 (zero, ~bitadder_1_out[0], ~bitadder_1_out[1], ~bitadder_1_out[2], ~bitadder_1_out[3], ~bitadder_1_out[4], ~bitadder_1_out[5]);  // AND_Gate
  BitAdder #(.width(32)) bitadder_1 (.in0(alu_out), .out(bitadder_1_out));
endmodule

module CONTROL_UNIT (
  input  in_1,
  input  [31:0] in_2,
  input  in_3,
  input  [31:0] in_4,
  output [31:0] pc,
  output [31:0] out_6,
  output [31:0] alub,
  output [4:0] RS2_OUT,
  output [4:0] RS1_OUT,
  output WE,
  output [4:0] RD_OUT,
  output [2:0] ALU_SELECT,
  output [19:0] ram_adr,
  output lw_inst,
  output sw_inst,
  output nop_inst
);

  wire and_1_out, and_2_out, and_3_out, and_4_out, and_5_out, and_6_out, and_7_out, and_8_out, and_9_out,
       and_10_out, and_13_out, and_16_out, and_17_out, and_18_out, and_19_out, and_20_out, and_21_out,
       and_22_out, and_23_out, and_24_out, or_1_out;
  wire [4:0] bitadder_1_out;
  wire [11:0] multiplexer_1_out;
  wire [19:0] bit_extender_3_out;
  wire [31:0] adder_1_out, bit_extender_1_out, bit_extender_2_out, multiplexer_3_out, multiplexer_4_out,
       subtractor_1_out;

  assign bit_extender_1_out = {{20{in_4[31]}}, in_4[31:20]};  // Bit_Extender bit_extender_1
  assign out_6 = sw_inst ? in_2 : 32'bz;  // Controlled_Buffer controlled_buffer_1
  and and_1 (and_1_out, ~in_4[12], ~in_4[13], ~in_4[14]);  // AND_Gate
  and and_2 (and_2_out, in_4[12], in_4[13], in_4[14]);
  and and_3 (and_3_out, ~in_4[12], in_4[13], in_4[14]);  // AND_Gate
  and and_4 (and_4_out, in_4[12], ~in_4[13], ~in_4[14]);  // AND_Gate
  and and_5 (and_5_out, ~in_4[12], ~in_4[13], in_4[14]);  // AND_Gate
  and and_6 (and_6_out, in_4[12], ~in_4[13], in_4[14]);  // AND_Gate
  BitAdder #(.width(25)) bitadder_1 (.in0(in_4[31:7]), .out(bitadder_1_out));
  Multiplexer #(.width(12), .enable("false")) multiplexer_1 (
    .in0(in_4[31:20]), .in1({in_4[31:25], in_4[11:7]}), .out(multiplexer_1_out), .sel(sw_inst));
  assign bit_extender_2_out = {{20{in_4[31]}}, {in_4[31:25], in_4[11:7]}};  // Bit_Extender bit_extender_2
  Multiplexer #(.width(32), .enable("false")) multiplexer_2 (
    .in0(in_2), .in1(bit_extender_1_out), .out(alub), .sel(and_8_out));
  assign ram_adr = or_1_out ? bit_extender_3_out : 20'bz;  // Controlled_Buffer controlled_buffer_2
  assign bit_extender_3_out = {{8{1'b0}}, multiplexer_1_out};  // Bit_Extender bit_extender_3
  Subtractor #(.width(32)) subtractor_1 (.a(bit_extender_2_out), .b(32'h1), .out(subtractor_1_out));  // open: bin, bout
  and and_7 (and_7_out, ~bitadder_1_out[0], ~bitadder_1_out[1], ~bitadder_1_out[2], ~bitadder_1_out[3], ~bitadder_1_out[4]);  // AND_Gate
  Multiplexer #(.width(32), .enable("false")) multiplexer_3 (
    .in0(bit_extender_2_out), .in1(subtractor_1_out), .out(multiplexer_3_out), .sel(bit_extender_2_out[31]));
  or or_1 (or_1_out, lw_inst, sw_inst);
  and and_8 (and_8_out, in_4[4], ~in_4[5], ~in_4[6]);  // AND_Gate
  and and_9 (and_9_out, in_4[4], in_4[5], ~in_4[6]);  // AND_Gate
  and and_10 (and_10_out, ~in_4[4], in_4[5], in_4[6]);  // AND_Gate
  and and_11 (lw_inst, ~in_4[4], ~in_4[5], ~in_4[6]);  // AND_Gate
  and and_12 (sw_inst, ~in_4[4], in_4[5], ~in_4[6]);  // AND_Gate
  and and_13 (and_13_out, and_10_out, ~in_3);  // AND_Gate
  Adder #(.width(32)) adder_1 (.a(pc), .b(multiplexer_4_out), .out(adder_1_out));  // open: cin, cout
  Multiplexer #(.width(32), .enable("false")) multiplexer_4 (
    .in0(32'h4), .in1(multiplexer_3_out), .out(multiplexer_4_out), .sel(and_13_out));
  or or_2 (WE, and_9_out, lw_inst, and_8_out);
  Register #(.width(32)) register_1 (.D(adder_1_out), .clk(in_1), .Q(pc));  // open: en, clr
  // AND_Gate and_14 has open pins: in0=and_8_out, in1=and_7_out, in2=and_1_out, out=open
  // AND_Gate and_15 has open pins: in0=and_1_out, in1=and_9_out, in2=in_4[30], out=open
  and and_16 (and_16_out, in_4[30], and_9_out, and_1_out);
  and and_17 (and_17_out, and_9_out, and_2_out);
  and and_18 (and_18_out, and_8_out, and_2_out);
  and and_19 (and_19_out, and_8_out, and_3_out);
  and and_20 (and_20_out, and_3_out, and_9_out);
  and and_21 (and_21_out, and_10_out, and_1_out);
  and and_22 (and_22_out, and_10_out, and_4_out);
  and and_23 (and_23_out, and_10_out, and_5_out);
  and and_24 (and_24_out, and_6_out, and_10_out);
  and and_25 (nop_inst, and_8_out, and_7_out);
  or or_3 (ALU_SELECT[0], and_16_out, and_23_out, and_21_out, and_20_out, and_19_out);
  or or_4 (ALU_SELECT[1], and_20_out, and_23_out, and_22_out, and_19_out, and_18_out, and_17_out);
  or or_5 (ALU_SELECT[2], and_21_out, and_22_out, and_23_out, and_24_out);

  assign RD_OUT = in_4[11:7];
  assign RS1_OUT = in_4[19:15];
  assign RS2_OUT = in_4[24:20];

  // Notes on the sheet:
  //   imm
  //   imm
  //   RB
  //   mem_data
endmodule

module RISCV32 (
  input  in_1
);

  wire alu32_1_zero, c, control_unit_1_lw_inst, control_unit_1_nop_inst, registerfile_1_p6,
       risc_vprogramrom_1_p3, risc_vprogramrom_1_p6;
  wire [2:0] control_unit_1_alu_select;
  wire [4:0] registerfile_1_p1, registerfile_1_p2, registerfile_1_p3;
  wire [19:0] control_unit_1_ram_adr;
  wire [31:0] alu32_1_alu_out, control_unit_1_alub, ram_1_data, registerfile_1_p4, registerfile_1_p5,
       risc_vprogramrom_1_p1, risc_vprogramrom_1_p2, risc_vprogramrom_1_p4;

  Clock clock_1 (.out(c));
  Multiplexer #(.width(32), .enable("false")) multiplexer_1 (
    .in0(alu32_1_alu_out), .in1(ram_1_data), .sel(control_unit_1_lw_inst));  // open: out
  RAM ram_1 (
    .addr(control_unit_1_ram_adr[7:0]), .data(ram_1_data[7:0]), .sel(1'b1), .clk(c),
    .ld(control_unit_1_lw_inst), .clr(in_1));
  // RISC_VProgramROM risc_vprogramrom_1: pin names not known; wires that end beside it: risc_vprogramrom_1_p1, risc_vprogramrom_1_p2, risc_vprogramrom_1_p3, risc_vprogramrom_1_p4, c, risc_vprogramrom_1_p6
  ALU32 alu32_1 (
    .zero(alu32_1_zero), .alu_out(alu32_1_alu_out), .in_B(control_unit_1_alub), .in_A(registerfile_1_p4),
    .alu_op(control_unit_1_alu_select));  // open: c
  // RegisterFile registerfile_1: pin names not known; wires that end beside it: registerfile_1_p1, registerfile_1_p2, registerfile_1_p3, registerfile_1_p4, registerfile_1_p5, registerfile_1_p6
  CONTROL_UNIT control_unit_1 (
    .RS2_OUT(registerfile_1_p3), .nop_inst(control_unit_1_nop_inst), .lw_inst(control_unit_1_lw_inst),
    .RS1_OUT(registerfile_1_p2), .ALU_SELECT(control_unit_1_alu_select), .sw_inst(risc_vprogramrom_1_p3),
    .in_4(risc_vprogramrom_1_p4), .RD_OUT(registerfile_1_p1), .WE(risc_vprogramrom_1_p6),
    .ram_adr(control_unit_1_ram_adr), .in_2(registerfile_1_p5), .out_6(risc_vprogramrom_1_p2),
    .in_3(alu32_1_zero), .pc(risc_vprogramrom_1_p1), .in_1(c), .alub(control_unit_1_alub));
  LED led_1 (.in(control_unit_1_nop_inst));
  LED led_2 (.in(registerfile_1_p6));
  // Pins of 1 and 4 bits meet at 4'b1111
  // Pins of 8 and 20 bits meet at control_unit_1_ram_adr
  // Pins of 8 and 32 bits meet at ram_1_data

  // Notes on the sheet:
  //   contents of risc_vprogramrom_1 (hex, n*v repeats v):
  //   addi x6, x0, 4 add  x7, x5, x6 sub  x8, x5, x6 and  x9, x8, x5 andi x10, x7, 9 or   x11, x6, x10 ori
  //   x12, x11, 3 label1: addi x6, x6, 1 sw x6, 1(x1) bne x6, x5, label1 beq x6, x5, label2 add  x7, x10,
  //   x6 sub  x8, x10, x6 and  x9, x10, x5 label2: blt x8, x6, label3 bge x8, x6, label3 sw  x1, 5(x3) lw
  //   x1, 3(x3) addi x1, x0, 22 addi x2, x0, 13 addi x3, x0, 420 label3: sw  x7, 2(x1) sw  x8, 3(x1) sw
  //   x9, 4(x1) lw  x2, 2(x1) lw  x3, 3(x1) lw  x4, 4(x1)
endmodule

module demo (
  output [31:0] out_1,
  output [31:0] out_2,
  output [31:0] out_3,
  output [31:0] out_4,
  output [31:0] out_5,
  output [31:0] out_6,
  output [4:0] out_7,
  output [4:0] out_8,
  output [4:0] out_9,
  output [2:0] out_10,
  output [19:0] out_11,
  output [31:0] out_12,
  output [31:0] out_13
);

  wire alu32_1_zero, c, control_unit_1_nop_inst, ram_1_p3, ram_1_p6, registerfile_1_p3;
  wire [31:0] multiplexer_1_out;

  Clock clock_1 (.out(c));
  // RAM ram_1: pin names not known; wires that end beside it: out_11, out_6, ram_1_p3, 4'b1111, c, ram_1_p6, out_3
  // RISC_VProgramROM risc_vprogramrom_1: pin names not known; wires that end beside it: out_13, out_12
  Multiplexer #(.width(32), .enable("false")) multiplexer_1 (
    .in0(out_1), .in1(out_3), .out(multiplexer_1_out), .sel(ram_1_p6));
  // RegisterFile registerfile_1: pin names not known; wires that end beside it: multiplexer_1_out, c, registerfile_1_p3, out_7, out_8, out_9, out_2, out_4
  CONTROL_UNIT control_unit_1 (
    .RS2_OUT(out_9), .nop_inst(control_unit_1_nop_inst), .lw_inst(ram_1_p6), .RS1_OUT(out_8),
    .ALU_SELECT(out_10), .sw_inst(ram_1_p3), .in_4(out_12), .RD_OUT(out_7), .WE(registerfile_1_p3),
    .ram_adr(out_11), .in_2(out_4), .out_6(out_6), .in_3(alu32_1_zero), .pc(out_13), .in_1(c), .alub(out_5));
  ALU32 alu32_1 (.zero(alu32_1_zero), .alu_out(out_1), .in_B(out_5), .in_A(out_2), .alu_op(out_10));  // open: c
  LED led_1 (.in(control_unit_1_nop_inst));

  // Notes on the sheet:
  //   contents of risc_vprogramrom_1 (hex, n*v repeats v):
  //   addi x6, x0, 43 addi x7, x0, 19 sw  x5, 1(x1) sw  x6, 2(x1) sw  x7, 3(x1) lw  x2, 1(x1) lw  x3,
  //   2(x1) lw  x4, 3(x1)
  //   MODELO DE PRUEBAS
endmodule
